// Digital circuit And_gate.dig as structural Verilog
module And_gate (
  input  in_1,
  input  in_2
);

  wire nfet_1_s, nfet_3_d, pullup_1_out;

  PullUp pullup_1 (.out(pullup_1_out));
  NFET nfet_1 (.G(in_1), .D(pullup_1_out), .S(nfet_1_s));
  NFET nfet_2 (.G(in_2), .D(nfet_1_s), .S(1'b0));
  NFET nfet_3 (.G(pullup_1_out), .D(nfet_3_d), .S(1'b0));
  PullUp pullup_2 (.out(nfet_3_d));
  LED led_1 (.in(nfet_3_d));
endmodule
