// Digital circuit Binary_clock.dig as structural Verilog
module Binary_clock (
  input  clk,
  input  in_2,
  input  in_3
);

  wire and_1_out, and_2_out, and_3_out, and_4_out, and_5_out, and_6_out, and_7_out, and_8_out, and_9_out,
       and_10_out, and_11_out, and_12_out, and_13_out, and_14_out, and_15_out, and_16_out, and_17_out,
       and_18_out, and_19_out, and_20_out, and_21_out, and_22_out, and_23_out, and_24_out, and_25_out,
       and_26_out, and_27_out, and_28_out, and_29_out, and_30_out, and_31_out, and_32_out, d_ff_1_q,
       d_ff_2_q, d_ff_3_q, d_ff_4_q, d_ff_5_q, d_ff_6_q, d_ff_7_q, d_ff_8_q, d_ff_9_q, d_ff_10_q, d_ff_11_q,
       jk_ff_as_1_q, jk_ff_as_2_q, jk_ff_as_3_q, jk_ff_as_4_q, jk_ff_as_5_q, jk_ff_as_6_q, jk_ff_as_7_q,
       jk_ff_as_8_q, jk_ff_as_9_q, jk_ff_as_10_q, jk_ff_as_11_q, jk_ff_as_12_q, jk_ff_as_13_q, jk_ff_as_14_q,
       jk_ff_as_15_q, jk_ff_as_16_q, jk_ff_as_17_q, jk_ff_as_18_q, jk_ff_as_19_q, jk_ff_as_20_q,
       jk_ff_as_21_q, jk_ff_as_22_q, jk_ff_as_23_q, jk_ff_as_24_q, jk_ff_as_25_q, jk_ff_as_26_q,
       jk_ff_as_27_q, jk_ff_as_28_q, jk_ff_as_29_q, jk_ff_as_30_q, jk_ff_as_31_q;

  JK_FF_AS jk_ff_as_1 (.Set(in_2), .J(1'b1), .C(clk), .K(1'b1), .Clr(in_3), .Q(jk_ff_as_1_q));  // open: nQ
  JK_FF_AS jk_ff_as_2 (
    .Set(in_2), .J(jk_ff_as_1_q), .C(clk), .K(jk_ff_as_1_q), .Clr(in_3), .Q(jk_ff_as_2_q));  // open: nQ
  and and_1 (and_1_out, jk_ff_as_1_q, jk_ff_as_2_q);
  JK_FF_AS jk_ff_as_3 (.Set(in_2), .J(and_1_out), .C(clk), .K(and_1_out), .Clr(in_3), .Q(jk_ff_as_3_q));  // open: nQ
  and and_2 (and_2_out, and_1_out, jk_ff_as_3_q);
  JK_FF_AS jk_ff_as_4 (.Set(in_2), .J(and_2_out), .C(clk), .K(and_2_out), .Clr(in_3), .Q(jk_ff_as_4_q));  // open: nQ
  and and_3 (and_3_out, and_2_out, jk_ff_as_4_q);
  JK_FF_AS jk_ff_as_5 (.Set(in_2), .J(and_3_out), .C(clk), .K(and_3_out), .Clr(in_3), .Q(jk_ff_as_5_q));  // open: nQ
  and and_4 (and_4_out, and_3_out, jk_ff_as_5_q);
  JK_FF_AS jk_ff_as_6 (.Set(in_2), .J(and_4_out), .C(clk), .K(and_4_out), .Clr(in_3), .Q(jk_ff_as_6_q));  // open: nQ
  and and_5 (and_5_out, and_4_out, jk_ff_as_6_q);
  JK_FF_AS jk_ff_as_7 (.Set(in_2), .J(and_5_out), .C(clk), .K(and_5_out), .Clr(in_3), .Q(jk_ff_as_7_q));  // open: nQ
  and and_6 (and_6_out, and_5_out, jk_ff_as_7_q);
  JK_FF_AS jk_ff_as_8 (.Set(in_2), .J(and_6_out), .C(clk), .K(and_6_out), .Clr(in_3), .Q(jk_ff_as_8_q));  // open: nQ
  and and_7 (and_7_out, and_6_out, jk_ff_as_8_q);
  JK_FF_AS jk_ff_as_9 (.Set(in_2), .J(and_7_out), .C(clk), .K(and_7_out), .Clr(in_3), .Q(jk_ff_as_9_q));  // open: nQ
  and and_8 (and_8_out, and_7_out, jk_ff_as_9_q);
  JK_FF_AS jk_ff_as_10 (.Set(in_2), .J(and_8_out), .C(clk), .K(and_8_out), .Clr(in_3), .Q(jk_ff_as_10_q));  // open: nQ
  and and_9 (and_9_out, and_8_out, jk_ff_as_10_q);
  JK_FF_AS jk_ff_as_11 (.Set(in_2), .J(and_9_out), .C(clk), .K(and_9_out), .Clr(in_3), .Q(jk_ff_as_11_q));  // open: nQ
  and and_10 (and_10_out, and_9_out, jk_ff_as_11_q);
  JK_FF_AS jk_ff_as_12 (
    .Set(in_2), .J(and_10_out), .C(clk), .K(and_10_out), .Clr(in_3), .Q(jk_ff_as_12_q));  // open: nQ
  and and_11 (and_11_out, and_10_out, jk_ff_as_12_q);
  JK_FF_AS jk_ff_as_13 (
    .Set(in_2), .J(and_11_out), .C(clk), .K(and_11_out), .Clr(in_3), .Q(jk_ff_as_13_q));  // open: nQ
  and and_12 (and_12_out, and_11_out, jk_ff_as_13_q);
  JK_FF_AS jk_ff_as_14 (
    .Set(in_2), .J(and_12_out), .C(clk), .K(and_12_out), .Clr(in_3), .Q(jk_ff_as_14_q));  // open: nQ
  and and_13 (and_13_out, and_12_out, jk_ff_as_14_q);
  LED led_1 (.in(jk_ff_as_15_q));
  JK_FF_AS jk_ff_as_15 (
    .Set(in_2), .J(and_13_out), .C(clk), .K(and_13_out), .Clr(d_ff_5_q), .Q(jk_ff_as_15_q));  // open: nQ
  and and_14 (and_14_out, and_13_out, jk_ff_as_15_q);
  LED led_2 (.in(jk_ff_as_16_q));
  JK_FF_AS jk_ff_as_16 (
    .Set(in_2), .J(and_14_out), .C(clk), .K(and_14_out), .Clr(d_ff_5_q), .Q(jk_ff_as_16_q));  // open: nQ
  and and_15 (and_15_out, and_14_out, jk_ff_as_16_q);
  JK_FF_AS jk_ff_as_17 (
    .Set(in_2), .J(and_15_out), .C(clk), .K(and_15_out), .Clr(d_ff_5_q), .Q(jk_ff_as_17_q));  // open: nQ
  LED led_3 (.in(jk_ff_as_17_q));
  and and_16 (and_16_out, and_15_out, jk_ff_as_17_q);
  JK_FF_AS jk_ff_as_18 (
    .Set(in_2), .J(and_16_out), .C(clk), .K(and_16_out), .Clr(d_ff_5_q), .Q(jk_ff_as_18_q));  // open: nQ
  LED led_4 (.in(jk_ff_as_18_q));
  and and_17 (and_17_out, and_16_out, jk_ff_as_18_q);
  D_FF d_ff_1 (.D(jk_ff_as_20_q), .C(clk), .Q(d_ff_1_q));  // open: nQ
  D_FF d_ff_2 (.D(jk_ff_as_19_q), .C(clk), .Q(d_ff_2_q));  // open: nQ
  D_FF d_ff_3 (.D(jk_ff_as_18_q), .C(clk), .Q(d_ff_3_q));  // open: nQ
  D_FF d_ff_4 (.D(jk_ff_as_17_q), .C(clk), .Q(d_ff_4_q));  // open: nQ
  LED led_5 (.in(jk_ff_as_19_q));
  JK_FF_AS jk_ff_as_19 (
    .Set(in_2), .J(and_17_out), .C(clk), .K(and_17_out), .Clr(d_ff_5_q), .Q(jk_ff_as_19_q));  // open: nQ
  and and_18 (and_18_out, and_17_out, jk_ff_as_19_q);
  and and_19 (and_19_out, d_ff_1_q, d_ff_2_q, d_ff_3_q, d_ff_4_q);
  LED led_6 (.in(jk_ff_as_20_q));
  JK_FF_AS jk_ff_as_20 (
    .Set(in_2), .J(and_18_out), .C(clk), .K(and_18_out), .Clr(d_ff_5_q), .Q(jk_ff_as_20_q));  // open: nQ
  and and_20 (and_20_out, jk_ff_as_20_q, and_19_out);
  D_FF d_ff_5 (.D(and_19_out), .C(clk), .Q(d_ff_5_q));  // open: nQ
  JK_FF_AS jk_ff_as_21 (
    .Set(in_2), .J(and_20_out), .C(clk), .K(and_20_out), .Clr(d_ff_10_q), .Q(jk_ff_as_21_q));  // open: nQ
  LED led_7 (.in(jk_ff_as_21_q));
  and and_21 (and_21_out, and_20_out, jk_ff_as_21_q);
  LED led_8 (.in(jk_ff_as_22_q));
  JK_FF_AS jk_ff_as_22 (
    .Set(in_2), .J(and_21_out), .C(clk), .K(and_21_out), .Clr(d_ff_10_q), .Q(jk_ff_as_22_q));  // open: nQ
  and and_22 (and_22_out, and_21_out, jk_ff_as_22_q);
  LED led_9 (.in(jk_ff_as_23_q));
  JK_FF_AS jk_ff_as_23 (
    .Set(in_2), .J(and_22_out), .C(clk), .K(and_22_out), .Clr(d_ff_10_q), .Q(jk_ff_as_23_q));  // open: nQ
  and and_23 (and_23_out, and_22_out, jk_ff_as_23_q);
  JK_FF_AS jk_ff_as_24 (
    .Set(in_2), .J(and_23_out), .C(clk), .K(and_23_out), .Clr(d_ff_10_q), .Q(jk_ff_as_24_q));  // open: nQ
  LED led_10 (.in(jk_ff_as_24_q));
  and and_24 (and_24_out, and_23_out, jk_ff_as_24_q);
  JK_FF_AS jk_ff_as_25 (
    .Set(in_2), .J(and_24_out), .C(clk), .K(and_24_out), .Clr(d_ff_10_q), .Q(jk_ff_as_25_q));  // open: nQ
  D_FF d_ff_6 (.D(jk_ff_as_26_q), .C(clk), .Q(d_ff_6_q));  // open: nQ
  D_FF d_ff_7 (.D(jk_ff_as_25_q), .C(clk), .Q(d_ff_7_q));  // open: nQ
  D_FF d_ff_8 (.D(jk_ff_as_24_q), .C(clk), .Q(d_ff_8_q));  // open: nQ
  D_FF d_ff_9 (.D(jk_ff_as_23_q), .C(clk), .Q(d_ff_9_q));  // open: nQ
  LED led_11 (.in(jk_ff_as_25_q));
  and and_25 (and_25_out, and_24_out, jk_ff_as_25_q);
  and and_26 (and_26_out, d_ff_6_q, d_ff_7_q, d_ff_8_q, d_ff_9_q);
  LED led_12 (.in(jk_ff_as_26_q));
  JK_FF_AS jk_ff_as_26 (
    .Set(in_2), .J(and_25_out), .C(clk), .K(and_25_out), .Clr(d_ff_10_q), .Q(jk_ff_as_26_q));  // open: nQ
  D_FF d_ff_10 (.D(and_26_out), .C(clk), .Q(d_ff_10_q));  // open: nQ
  and and_27 (and_27_out, jk_ff_as_26_q, and_26_out);
  LED led_13 (.in(jk_ff_as_27_q));
  JK_FF_AS jk_ff_as_27 (
    .Set(in_2), .J(and_27_out), .C(clk), .K(and_27_out), .Clr(d_ff_11_q), .Q(jk_ff_as_27_q));  // open: nQ
  and and_28 (and_28_out, and_27_out, jk_ff_as_27_q);
  LED led_14 (.in(jk_ff_as_28_q));
  JK_FF_AS jk_ff_as_28 (
    .Set(in_2), .J(and_28_out), .C(clk), .K(and_28_out), .Clr(d_ff_11_q), .Q(jk_ff_as_28_q));  // open: nQ
  and and_29 (and_29_out, and_28_out, jk_ff_as_28_q);
  JK_FF_AS jk_ff_as_29 (
    .Set(in_2), .J(and_29_out), .C(clk), .K(and_29_out), .Clr(d_ff_11_q), .Q(jk_ff_as_29_q));  // open: nQ
  LED led_15 (.in(jk_ff_as_29_q));
  and and_30 (and_30_out, and_29_out, jk_ff_as_29_q);
  JK_FF_AS jk_ff_as_30 (
    .Set(in_2), .J(and_30_out), .C(clk), .K(and_30_out), .Clr(d_ff_11_q), .Q(jk_ff_as_30_q));  // open: nQ
  LED led_16 (.in(jk_ff_as_30_q));
  and and_31 (and_31_out, and_30_out, jk_ff_as_30_q);
  and and_32 (and_32_out, jk_ff_as_30_q, jk_ff_as_31_q);
  LED led_17 (.in(jk_ff_as_31_q));
  JK_FF_AS jk_ff_as_31 (
    .Set(in_2), .J(and_31_out), .C(clk), .K(and_31_out), .Clr(d_ff_11_q), .Q(jk_ff_as_31_q));  // open: nQ
  D_FF d_ff_11 (.D(and_32_out), .C(clk), .Q(d_ff_11_q));  // open: nQ

  // Notes on the sheet:
  //   clk: Hz: 16384
endmodule
