// Digital circuit d-flip-flop.dig as structural Verilog
module d_flip_flop (
  input  clk,
  input  D,
  output Q,
  output Q_2
);

  wire nfet_1_d, nfet_2_d, nfet_2_s, nfet_4_d, nfet_4_s, nfet_6_s, nfet_8_s;

  NFET nfet_1 (.G(D), .D(nfet_1_d), .S(1'b0));
  NFET nfet_2 (.G(D), .D(nfet_2_d), .S(nfet_2_s));
  NFET nfet_3 (.G(clk), .D(nfet_2_s), .S(1'b0));
  PullUp pullup_1 (.out(nfet_1_d));
  NFET nfet_4 (.G(clk), .D(nfet_4_d), .S(nfet_4_s));
  NFET nfet_5 (.G(nfet_1_d), .D(nfet_4_s), .S(1'b0));
  PullUp pullup_2 (.out(nfet_2_d));
  PullUp pullup_3 (.out(nfet_4_d));
  PullUp pullup_4 (.out(Q));
  NFET nfet_6 (.G(nfet_2_d), .D(Q), .S(nfet_6_s));
  NFET nfet_7 (.G(Q_2), .D(nfet_6_s), .S(1'b0));
  PullUp pullup_5 (.out(Q_2));
  NFET nfet_8 (.G(Q), .D(Q_2), .S(nfet_8_s));
  NFET nfet_9 (.G(nfet_4_d), .D(nfet_8_s), .S(1'b0));
endmodule
