// Digital circuit jk-flip-flop.dig as structural Verilog
module jk_flip_flop (
  input  j,
  input  k,
  input  clk,
  output out_3,
  output out_4
);

  wire nfet_1_s, nfet_2_s, nfet_4_s, nfet_5_s, nfet_7_s, nfet_9_s, pullup_1_out, pullup_2_out;

  PullUp pullup_1 (.out(pullup_1_out));
  NFET nfet_1 (.G(out_4), .D(pullup_1_out), .S(nfet_1_s));
  NFET nfet_2 (.G(j), .D(nfet_1_s), .S(nfet_2_s));
  NFET nfet_3 (.G(clk), .D(nfet_2_s), .S(1'b0));
  PullUp pullup_2 (.out(pullup_2_out));
  NFET nfet_4 (.G(clk), .D(pullup_2_out), .S(nfet_4_s));
  NFET nfet_5 (.G(k), .D(nfet_4_s), .S(nfet_5_s));
  NFET nfet_6 (.G(out_3), .D(nfet_5_s), .S(1'b0));
  PullUp pullup_3 (.out(out_3));
  NFET nfet_7 (.G(pullup_1_out), .D(out_3), .S(nfet_7_s));
  NFET nfet_8 (.G(out_4), .D(nfet_7_s), .S(1'b0));
  PullUp pullup_4 (.out(out_4));
  NFET nfet_9 (.G(out_3), .D(out_4), .S(nfet_9_s));
  NFET nfet_10 (.G(pullup_2_out), .D(nfet_9_s), .S(1'b0));
endmodule
